# Fritzing sketch moock-clock-v3 (saved by Fritzing 0.9.4)
circuit board: 7.98787cm x 7.05435cm
breadboards: 1

parts:
  Part1 = Arduino Nano (Rev3.0)
  BAT1 = BC9VPC [part_number="12 V DC" package=bc9vpc]
  S1 = Momentary Switch [package=ksa_sealed_tac_switch]
  S2 = Momentary Switch [package=ksa_sealed_tac_switch]
  LED1 = LED - 5mm [color="Red (633nm)" package="5 mm [THT]"]
  R9 = Resistor [tolerance=±5% resistance=10k package=THT]
  R10 = Resistor [tolerance=±5% resistance=10k package=THT]
  R11 = Resistor [tolerance=±5% resistance=10k package=THT]
  R12 = Resistor [tolerance=±5% resistance=10k package=THT]
  R13 = Resistor [tolerance=±5% resistance=10k package=THT]
  R14 = Resistor [tolerance=±5% resistance=10k package=THT]
  R15 = Resistor [tolerance=±5% resistance=10k package=THT]
  R16 = Resistor [tolerance=±5% resistance=10k package=THT]
  Q1 = Basic FET N-Channel [part_number=FQP30N06L package="TO220 [THT]"]
  Q2 = Basic FET N-Channel [part_number=FQP30N06L package="TO220 [THT]"]
  Q3 = Basic FET N-Channel [part_number=FQP30N06L package="TO220 [THT]"]
  Q4 = Basic FET N-Channel [part_number=FQP30N06L package="TO220 [THT]"]
  Q5 = Basic FET N-Channel [part_number=FQP30N06L package="TO220 [THT]"]
  Q6 = Basic FET N-Channel [part_number=FQP30N06L package="TO220 [THT]"]
  Q7 = Basic FET N-Channel [part_number=FQP30N06L package="TO220 [THT]"]
  Q8 = Basic FET N-Channel [part_number=FQP30N06L package="TO220 [THT]"]
  GND1 = female pin header, 1 pin [form="♀ (female)"]
  GND2 = female pin header, 1 pin [form="♀ (female)"]
  GND3 = female pin header, 1 pin [form="♀ (female)"]
  GND4 = female pin header, 1 pin [form="♀ (female)"]
  GND5 = female pin header, 1 pin [form="♀ (female)"]
  GND6 = female pin header, 1 pin [form="♀ (female)"]
  GND7 = female pin header, 1 pin [form="♀ (female)"]
  GND8 = female pin header, 1 pin [form="♀ (female)"]
  GND9 = female pin header, 1 pin [form="♀ (female)"]
  GND10 = female pin header, 1 pin [form="♀ (female)"]
  ZS-042_RTC1 = ZS-042 RTC Module
  Segments_6_to_8_and_Vcc = female pin header, 5 pins [form="♀ (female)"]
  Segments_1_to_5 = female pin header, 5 pins [form="♀ (female)"]
  TM1637 = rounded female pin header, 4 pins [form="♀ (female rounded)"]
  TM1637_2 = male pin header, 4 pins [form="♂ (male)"]
  TM1637_3 = female pin header, 4 pins [form="♀ (female)" part_number=TM1632]

nets:
  GND: Part1.GND, BAT1.V-, S1.1, S2.1, LED1.cathode, R9.Pin_0, R10.Pin_0, R11.Pin_0, R12.Pin_0, R13.Pin_0, R14.Pin_0, R15.Pin_0, R16.Pin_0, Q1.source, Q2.source, Q3.source, Q4.source, Q5.source, Q6.source, Q7.source, Q8.source, GND1.pin1, GND2.pin1, GND3.pin1, GND4.pin1, GND5.pin1, GND6.pin1, GND7.pin1, GND8.pin1, GND9.pin1, GND10.pin1, ZS-042_RTC1.GND, TM1637.pin3, TM1637_2.pin3, TM1637_3.pin3
  N1: Part1.D2, TM1637.pin2, TM1637_2.pin2, TM1637_3.pin2
  N2: Part1.D3, TM1637.pin1, TM1637_2.pin1, TM1637_3.pin1
  N3: Part1.D4, S1.3
  N4: Part1.D5, S2.3
  N5: Part1.D6, R9.Pin_1, Q1.gate
  N6: Part1.D7, R10.Pin_1, Q2.gate
  N7: Part1.D8, R11.Pin_1, Q3.gate
  N8: Part1.D9, R12.Pin_1, Q4.gate
  N9: Part1.D10, R13.Pin_1, Q5.gate
  N10: Part1.D11/MOSI, R14.Pin_1, Q6.gate
  N11: Part1.D12/MISO, R16.Pin_1, Q7.gate
  N12: Part1.VIN, BAT1.V+, Segments_6_to_8_and_Vcc.pin5
  5V: Part1.5V, ZS-042_RTC1.VCC, TM1637.pin4, TM1637_2.pin4, TM1637_3.pin4
  N13: Part1.A5, ZS-042_RTC1.SCL
  N14: Part1.A4, ZS-042_RTC1.SDA
  N15: Part1.A0, LED1.anode
  N16: Part1.D13/SCK, R15.Pin_1, Q8.gate
  N17: Q1.drain, Segments_1_to_5.pin1
  N18: Q2.drain, Segments_1_to_5.pin2
  N19: Q3.drain, Segments_1_to_5.pin3
  N20: Q4.drain, Segments_1_to_5.pin4
  N21: Q5.drain, Segments_1_to_5.pin5
  N22: Q6.drain, Segments_6_to_8_and_Vcc.pin1
  N23: Q7.drain, Segments_6_to_8_and_Vcc.pin2
  N24: Q8.drain, Segments_6_to_8_and_Vcc.pin3
